// Digital circuit CPU 16.dig as structural Verilog
module CPU_16 (
  input  Clock,
  input  nWAIT,
  output CLK1,
  output CLK2
);

  wire _74245_1_p13, _74245_1_p14, _74245_1_p15, _74245_1_p16, _74245_1_p17, _74245_1_p18, _74245_1_p19,
       _74245_1_p20, _74245_2_p13, _74245_2_p14, _74245_2_p15, _74245_2_p16, _74245_2_p17, _74245_2_p18,
       _74245_2_p19, _74245_2_p20, and_1_out, and_2_out, and_3_out, and_8_out, and_9_out, and_10_out,
       and_13_out, and_14_out, and_15_out, bussplitter_1_d2, bussplitter_1_d3, bussplitter_1_d4,
       bussplitter_1_d5, bussplitter_1_d6, bussplitter_1_d7, bussplitter_1_d8, bussplitter_1_d9,
       bussplitter_1_d10, bussplitter_1_d11, bussplitter_1_d12, bussplitter_1_d13, bussplitter_1_d14,
       bussplitter_1_d15, COND_C, COND_N, COND_NEG, COND_POS, COND_RES, COND_Z, CONV_V,
       demultiplexer_1_out_0, demultiplexer_1_out_1, demultiplexer_2_out_1, demultiplexer_2_out_2,
       demultiplexer_2_out_3, demultiplexer_2_out_4, demultiplexer_2_out_5, demultiplexer_4_out_0,
       demultiplexer_4_out_1, demultiplexer_4_out_2, demultiplexer_5_out_1, demultiplexer_5_out_2,
       demultiplexer_5_out_3, demultiplexer_5_out_4, demultiplexer_5_out_5, demultiplexer_5_out_6,
       demultiplexer_5_out_7, demultiplexer_6_out_0, demultiplexer_6_out_1, demultiplexer_6_out_2,
       demultiplexer_6_out_3, demultiplexer_6_out_4, demultiplexer_6_out_5, demultiplexer_6_out_6,
       demultiplexer_6_out_7, demultiplexer_7_out_0, demultiplexer_8_out_1, demultiplexer_8_out_2,
       demultiplexer_8_out_3, demultiplexer_9_out_0, demultiplexer_9_out_1, demultiplexer_9_out_2,
       demultiplexer_9_out_3, demultiplexer_9_out_4, demultiplexer_9_out_5, demultiplexer_9_out_6,
       demultiplexer_9_out_7, demultiplexer_10_out_0, demultiplexer_10_out_1, demultiplexer_10_out_2,
       demultiplexer_10_out_3, demultiplexer_10_out_4, demultiplexer_10_out_5, demultiplexer_10_out_6,
       demultiplexer_10_out_7, demultiplexer_11_out_0, demultiplexer_11_out_1, demultiplexer_11_out_2,
       demultiplexer_12_out_1, demultiplexer_12_out_2, demultiplexer_12_out_3, demultiplexer_12_out_4,
       demultiplexer_12_out_5, demultiplexer_12_out_6, demultiplexer_12_out_7, demultiplexer_13_out_0,
       demultiplexer_13_out_1, demultiplexer_13_out_2, demultiplexer_13_out_3, demultiplexer_13_out_4,
       demultiplexer_13_out_5, demultiplexer_13_out_6, demultiplexer_13_out_7, demultiplexer_14_out_0,
       demultiplexer_14_out_1, demultiplexer_15_out_1, demultiplexer_15_out_2, demultiplexer_15_out_3,
       demultiplexer_15_out_4, FLAG_C, FLAG_V, HLT, HLT_ack, IRQ0_any, IRQ_0, IRQ_ack, IRQ_FTdat, IRQ_REQ,
       keyboard_1_av, MEM_dir, nA_DATout, nA_st, nB_DATout, nB_st, nC_DATout, nC_Fst, nC_st, nD_DATout,
       nD_st, nE_DATout, nE_st, nF_ALUin, nF_DATin, nF_DATout, nIR_st, nIRQ_en, nIRQ_Fst, nLSH_DATout,
       nMAR_ADSout, nMARH_st, nMARL_st, nMDR_DATout, nMDR_st, nMEM_DATout, nMEM_en, nMEM_st, nMSK_st,
       nNZ_Fst, nOP1_st, nOP2_st, nor_1_out, nor_2_out, nor_3_out, nor_4_out, nor_5_out, nor_6_out,
       nor_7_out, nor_8_out, nor_9_out, nor_10_out, not_1_out, not_2_out, not_3_out, not_4_out, not_5_out,
       not_8_out, not_9_out, not_23_out, not_26_out, not_38_out, not_39_out, not_40_out, not_41_out,
       not_42_out, not_43_out, not_44_out, not_45_out, not_46_out, not_47_out, not_48_out, not_50_out,
       not_51_out, not_58_out, not_59_out, not_60_out, not_62_out, not_84_out, not_85_out, not_86_out,
       not_87_out, nPAN_HLTen, nPC_ADSout, nPC_DATout, nPC_en, nPC_st, nRSH_DATout, nRST, nRST_SEQen,
       nSEQ_en, nSEQ_st, nSEX_DATout, nSP_ADSout, nSP_DATout, nSP_en, nSP_st, nSUM_DATout, nV_Fst,
       nWRD_DATout, nX_DATout, nX_en, nX_st, nY_DATout, nY_en, nY_st, or_2_out, or_3_out, or_4_out, or_5_out,
       or_6_out, or_7_out, or_8_out, pulldown_5_out, pulldown_6_out, REG_dir, RESET_out, RST_ack, RST_IRen,
       RUN_out, SEQ_val, STP, t_ff_1_nq, t_ff_1_q, TEMP_clr, \Σ_Csel , \Σ_Cval , \Σ_M ;
  wire [1:0] FLAG_NZ;
  wire [2:0] AOUT_sel, COND_sel;
  wire [3:0] alu_1_c_f, driverinvsel_10_out, FST_sel, \µSEQ_out , \Σ_sel ;
  wire [4:0] DOUT_sel, ST_sel;
  wire [5:4] HLT_q;
  wire [7:0] MARH_out, MARL_out, MSK_q;
  wire [15:0] _15_out, A_q, ADDRESS, alu_1_sum, B_q, barrelshifter_1_out, barrelshifter_2_out,
       bitextender_1_out, C_q, d_ff_1_q, d_ff_2_q, D_q, DATA, E_q, IR_q, MDR_q, MEMDATA, OP1_q, OP2_out,
       PC_out, pulldown_2_out, SP_out, X_out, Y_out;
  wire [47:0] \µCODE_d ;
  wire [47:29] CTRL_q;

  not not_1 (not_1_out, COND_RES);
  Demultiplexer demultiplexer_1 (
    .sel(FST_sel[3]), .in(1'b1), .out_0(demultiplexer_1_out_0), .out_1(demultiplexer_1_out_1));
  and and_1 (and_1_out, nSEQ_st, not_1_out);
  Register IRQ (.D(DATA[4]), .C(CLK2), .en(~nIRQ_Fst), .Q(IRQ_FTdat));
  assign DATA = ~nWRD_DATout ? {16{1'b1}} : 16'bz;  // DriverInvSel driverinvsel_1
  and and_2 (and_2_out, nSEQ_en, nRST_SEQen);
  buf and_3 (and_3_out, and_1_out);  // And open: In_2
  Demultiplexer #(.Selector_Bits(3)) demultiplexer_2 (
    .sel(FST_sel[2:0]), .in(demultiplexer_1_out_0), .out_1(demultiplexer_2_out_1),
    .out_2(demultiplexer_2_out_2), .out_3(demultiplexer_2_out_3), .out_4(demultiplexer_2_out_4),
    .out_5(demultiplexer_2_out_5));  // open: out_0, out_6, out_7
  Demultiplexer #(.Selector_Bits(3)) demultiplexer_3 (
    .sel(FST_sel[2:0]), .in(demultiplexer_1_out_1));  // open: out_0, out_1, out_2, out_3, out_4, out_5, out_6, out_7
  Register #(.Bits(8)) MSK (.D(MEMDATA[7:0]), .C(CLK2), .en(~nMSK_st), .Q(MSK_q));
  PullUp pullup_1 (.out(HLT));
  nor nor_1 (nor_1_out, HLT, RST_IRen);
  nor nor_2 (nor_2_out, IRQ_REQ, IRQ_FTdat);
  not not_2 (not_2_out, demultiplexer_2_out_1);
  not not_3 (not_3_out, demultiplexer_2_out_2);
  not not_4 (not_4_out, demultiplexer_2_out_3);
  not not_5 (not_5_out, demultiplexer_2_out_4);
  not not_6 (nIRQ_Fst, demultiplexer_2_out_5);
  PullDown #(.Bits(16)) pulldown_1 (.out(DATA));
  PullDown #(.Bits(12)) pulldown_2 (.out(pulldown_2_out[11:0]));
  assign pulldown_2_out[11:0] = ~RST_IRen ? DATA[11:0] : 12'bz;  // DriverInvSel driverinvsel_2
  and and_4 (nNZ_Fst, not_2_out, not_5_out);
  and and_5 (nV_Fst, not_3_out, not_5_out);
  and and_6 (nC_Fst, not_4_out, not_5_out);
  nor nor_3 (nor_3_out, MSK_q[0], IRQ_0);
  nor nor_4 (nor_4_out, MSK_q[1], 1'b1);
  nor nor_5 (nor_5_out, MSK_q[2], 1'b1);
  nor nor_6 (nor_6_out, MSK_q[3], 1'b1);
  nor nor_7 (nor_7_out, MSK_q[4], 1'b1);
  nor nor_8 (nor_8_out, MSK_q[5], 1'b1);
  nor nor_9 (nor_9_out, MSK_q[6], 1'b1);
  nor nor_10 (nor_10_out, MSK_q[7], 1'b1);
  CounterPreset #(.Bits(4)) \u_µSEQ  (
    .en(~and_2_out), .C(CLK2), .dir(1'b0), .in({3'b000, SEQ_val}), .ld(~and_3_out), .clr(1'b0),
    .out(\µSEQ_out ));  // open: ovf
  Register u_HLT (.D(nor_1_out), .C(CLK2), .en(~1'b0), .Q(HLT_q[4]));
  Register IRQ_2 (.D(nor_2_out), .C(CLK2), .en(~nIRQ_en), .Q(HLT_q[5]));
  Register #(.Bits(16)) IR (.D(pulldown_2_out), .C(CLK2), .en(~nIR_st), .Q(IR_q));
  not not_7 (nRST, RESET_out);
  DipSwitch RESET (.out(RESET_out));
  Demultiplexer #(.Selector_Bits(2)) demultiplexer_4 (
    .sel(ST_sel[4:3]), .in(1'b1), .out_0(demultiplexer_4_out_0), .out_1(demultiplexer_4_out_1),
    .out_2(demultiplexer_4_out_2));  // open: out_3
  PriorityEncoder #(.Selector_Bits(3)) IRQ0 (
    .in0(nor_3_out), .in1(nor_4_out), .in2(nor_5_out), .in3(nor_6_out), .in4(nor_7_out), .in5(nor_8_out),
    .in6(nor_9_out), .in7(nor_10_out), .any(IRQ0_any));  // open: num
  ROM #(.AddrBits(18), .Bits(48)) \u_µCODE  (.A({IR_q[11:0], HLT_q, \µSEQ_out }), .sel(1'b1), .D(\µCODE_d ));
  not not_8 (not_8_out, TEMP_clr);
  not not_9 (not_9_out, RST_ack);
  not not_10 (IRQ_REQ, IRQ0_any);
  // _7474 _7474_1: pin names not known; wires that end beside it: nRST, 1'b0, 1'b0, not_8_out, nRST, 1'b0, 1'b0, not_9_out, 1'b1, 1'b0, nRST_SEQen, RST_IRen
  Demultiplexer #(.Selector_Bits(3)) demultiplexer_5 (
    .sel(ST_sel[2:0]), .in(demultiplexer_4_out_0), .out_1(demultiplexer_5_out_1),
    .out_2(demultiplexer_5_out_2), .out_3(demultiplexer_5_out_3), .out_4(demultiplexer_5_out_4),
    .out_5(demultiplexer_5_out_5), .out_6(demultiplexer_5_out_6), .out_7(demultiplexer_5_out_7));  // open: out_0
  Demultiplexer #(.Selector_Bits(3)) demultiplexer_6 (
    .sel(ST_sel[2:0]), .in(demultiplexer_4_out_1), .out_0(demultiplexer_6_out_0),
    .out_1(demultiplexer_6_out_1), .out_2(demultiplexer_6_out_2), .out_3(demultiplexer_6_out_3),
    .out_4(demultiplexer_6_out_4), .out_5(demultiplexer_6_out_5), .out_6(demultiplexer_6_out_6),
    .out_7(demultiplexer_6_out_7));
  Demultiplexer #(.Selector_Bits(3)) demultiplexer_7 (
    .sel(ST_sel[2:0]), .in(demultiplexer_4_out_2), .out_0(demultiplexer_7_out_0));  // open: out_1, out_2, out_3, out_4, out_5, out_6, out_7
  Demultiplexer #(.Selector_Bits(3)) demultiplexer_8 (
    .sel(AOUT_sel), .in(1'b1), .out_1(demultiplexer_8_out_1), .out_2(demultiplexer_8_out_2),
    .out_3(demultiplexer_8_out_3));  // open: out_0, out_4, out_5, out_6, out_7
  D_FF #(.Bits(48)) CTRL (
    .D(\µCODE_d ), .C(CLK1),
    .Q({CTRL_q[47:44], RST_ack, CTRL_q[42], MEM_dir, CTRL_q[40:39], IRQ_ack, HLT_ack, CTRL_q[36], TEMP_clr, SEQ_val, CTRL_q[33:32], nF_ALUin, CTRL_q[30:29], REG_dir, COND_POS, \Σ_Cval , \Σ_Csel , \Σ_M , \Σ_sel , COND_sel, FST_sel, AOUT_sel, DOUT_sel, ST_sel}));  // open: nQ
  not not_11 (nA_st, demultiplexer_5_out_1);
  not not_12 (nB_st, demultiplexer_5_out_2);
  not not_13 (nC_st, demultiplexer_5_out_3);
  not not_14 (nD_st, demultiplexer_5_out_4);
  not not_15 (nE_st, demultiplexer_5_out_5);
  not not_16 (nX_st, demultiplexer_5_out_6);
  not not_17 (nY_st, demultiplexer_5_out_7);
  not not_18 (nSP_st, demultiplexer_6_out_0);
  not not_19 (nPC_st, demultiplexer_6_out_1);
  not not_20 (nOP1_st, demultiplexer_6_out_2);
  not not_21 (nOP2_st, demultiplexer_6_out_3);
  not not_22 (nIR_st, demultiplexer_6_out_4);
  not not_23 (not_23_out, demultiplexer_6_out_5);
  not not_24 (nMARH_st, demultiplexer_6_out_6);
  not not_25 (nMDR_st, demultiplexer_6_out_7);
  not not_26 (not_26_out, demultiplexer_7_out_0);
  not not_27 (nSP_ADSout, demultiplexer_8_out_1);
  not not_28 (nPC_ADSout, demultiplexer_8_out_2);
  not not_29 (nMAR_ADSout, demultiplexer_8_out_3);
  assign nMEM_st = CLK2 ? not_26_out : 1'bz;  // Driver driver_1
  not not_30 (nSP_en, CTRL_q[29]);
  not not_31 (nPC_en, CTRL_q[30]);
  not not_32 (nSEQ_en, CTRL_q[32]);
  not not_33 (nSEQ_st, CTRL_q[33]);
  not not_34 (nIRQ_en, CTRL_q[36]);
  not not_35 (nX_en, CTRL_q[39]);
  not not_36 (nY_en, CTRL_q[40]);
  not not_37 (nMEM_en, CTRL_q[42]);
  Demultiplexer #(.Selector_Bits(3)) demultiplexer_9 (
    .sel(ADDRESS[15:13]), .in(not_38_out), .out_0(demultiplexer_9_out_0), .out_1(demultiplexer_9_out_1),
    .out_2(demultiplexer_9_out_2), .out_3(demultiplexer_9_out_3), .out_4(demultiplexer_9_out_4),
    .out_5(demultiplexer_9_out_5), .out_6(demultiplexer_9_out_6), .out_7(demultiplexer_9_out_7));
  not not_38 (not_38_out, nMEM_en);
  Demultiplexer #(.Selector_Bits(3)) demultiplexer_10 (
    .sel(ADDRESS[6:4]), .in(not_39_out), .out_0(demultiplexer_10_out_0), .out_1(demultiplexer_10_out_1),
    .out_2(demultiplexer_10_out_2), .out_3(demultiplexer_10_out_3), .out_4(demultiplexer_10_out_4),
    .out_5(demultiplexer_10_out_5), .out_6(demultiplexer_10_out_6), .out_7(demultiplexer_10_out_7));
  not not_39 (not_39_out, not_46_out);
  and and_7 (nMARL_st, nMARH_st, not_23_out);
  not not_40 (not_40_out, demultiplexer_9_out_0);
  not not_41 (not_41_out, demultiplexer_9_out_1);
  not not_42 (not_42_out, demultiplexer_9_out_2);
  not not_43 (not_43_out, demultiplexer_9_out_3);
  not not_44 (not_44_out, demultiplexer_9_out_4);
  not not_45 (not_45_out, demultiplexer_9_out_5);
  not not_46 (not_46_out, demultiplexer_9_out_6);
  not not_47 (not_47_out, demultiplexer_9_out_7);
  not not_48 (not_48_out, demultiplexer_10_out_0);
  // Not not_49 has open pins: in=demultiplexer_10_out_1, out=open
  not not_50 (not_50_out, demultiplexer_10_out_2);
  not not_51 (not_51_out, demultiplexer_10_out_3);
  // Not not_52 has open pins: in=demultiplexer_10_out_4, out=open
  // Not not_53 has open pins: in=demultiplexer_10_out_5, out=open
  // Not not_54 has open pins: in=demultiplexer_10_out_6, out=open
  // Not not_55 has open pins: in=demultiplexer_10_out_7, out=open
  not not_56 (COND_NEG, COND_POS);
  not not_57 (nF_DATin, nF_ALUin);
  or or_1 (nMSK_st, nMEM_st, not_48_out);
  or or_2 (or_2_out, not_40_out, not_41_out, not_42_out, not_43_out, not_44_out, not_45_out);
  Terminal terminal_1 (.D(DATA[7:0]), .C(CLK2), .en(not_58_out));
  not not_58 (not_58_out, not_50_out);
  Keyboard keyboard_1 (.C(CLK2), .en(not_59_out), .D(MEMDATA), .av(keyboard_1_av));
  not not_59 (not_59_out, not_51_out);
  Demultiplexer #(.Selector_Bits(2)) demultiplexer_11 (
    .sel(DOUT_sel[4:3]), .in(1'b1), .out_0(demultiplexer_11_out_0), .out_1(demultiplexer_11_out_1),
    .out_2(demultiplexer_11_out_2));  // open: out_3
  not not_60 (not_60_out, not_47_out);
  not not_61 (IRQ_0, keyboard_1_av);
  and and_8 (and_8_out, ~COND_N, FLAG_NZ[0]);  // And
  not not_62 (not_62_out, Clock);
  PullDown pulldown_3 (.out(Clock));
  ROM #(.AddrBits(16), .Bits(16)) ROM_16x64k (.A(ADDRESS), .sel(not_60_out), .D(MEMDATA));
  RAMSinglePortSel #(.AddrBits(16), .Bits(16)) RAM0_16x64k (
    .A(ADDRESS), .CS(~or_2_out), .WE(~nMEM_st), .OE(~nMEM_DATout), .D(MEMDATA));
  and and_9 (and_9_out, ~COND_Z, FLAG_NZ[1]);  // And
  T_FF #(.withEnable("false")) t_ff_1 (.C(not_62_out), .Q(t_ff_1_q), .nQ(t_ff_1_nq));
  Demultiplexer #(.Selector_Bits(3)) demultiplexer_12 (
    .sel(DOUT_sel[2:0]), .in(demultiplexer_11_out_0), .out_1(demultiplexer_12_out_1),
    .out_2(demultiplexer_12_out_2), .out_3(demultiplexer_12_out_3), .out_4(demultiplexer_12_out_4),
    .out_5(demultiplexer_12_out_5), .out_6(demultiplexer_12_out_6), .out_7(demultiplexer_12_out_7));  // open: out_0
  Demultiplexer #(.Selector_Bits(3)) demultiplexer_13 (
    .sel(DOUT_sel[2:0]), .in(demultiplexer_11_out_1), .out_0(demultiplexer_13_out_0),
    .out_1(demultiplexer_13_out_1), .out_2(demultiplexer_13_out_2), .out_3(demultiplexer_13_out_3),
    .out_4(demultiplexer_13_out_4), .out_5(demultiplexer_13_out_5), .out_6(demultiplexer_13_out_6),
    .out_7(demultiplexer_13_out_7));
  Demultiplexer #(.Selector_Bits(3)) demultiplexer_14 (
    .sel(DOUT_sel[2:0]), .in(demultiplexer_11_out_2), .out_0(demultiplexer_14_out_0),
    .out_1(demultiplexer_14_out_1));  // open: out_2, out_3, out_4, out_5, out_6, out_7
  Demultiplexer #(.Selector_Bits(3)) demultiplexer_15 (
    .sel(COND_sel), .in(1'b1), .out_1(demultiplexer_15_out_1), .out_2(demultiplexer_15_out_2),
    .out_3(demultiplexer_15_out_3), .out_4(demultiplexer_15_out_4));  // open: out_0, out_5, out_6, out_7
  PullDown #(.Bits(16)) pulldown_4 (.out(MEMDATA));
  and and_10 (and_10_out, ~CONV_V, FLAG_V);  // And
  and and_11 (CLK1, Clock, t_ff_1_q);
  and and_12 (CLK2, t_ff_1_nq, ~nWAIT, Clock);  // And
  not not_63 (nA_DATout, demultiplexer_12_out_1);
  not not_64 (nB_DATout, demultiplexer_12_out_2);
  not not_65 (nC_DATout, demultiplexer_12_out_3);
  not not_66 (nD_DATout, demultiplexer_12_out_4);
  not not_67 (nE_DATout, demultiplexer_12_out_5);
  not not_68 (nX_DATout, demultiplexer_12_out_6);
  not not_69 (nY_DATout, demultiplexer_12_out_7);
  not not_70 (nF_DATout, demultiplexer_13_out_0);
  not not_71 (nSP_DATout, demultiplexer_13_out_1);
  not not_72 (nPC_DATout, demultiplexer_13_out_2);
  not not_73 (nSUM_DATout, demultiplexer_13_out_3);
  not not_74 (nLSH_DATout, demultiplexer_13_out_4);
  not not_75 (nRSH_DATout, demultiplexer_13_out_5);
  not not_76 (nSEX_DATout, demultiplexer_13_out_6);
  not not_77 (nMEM_DATout, demultiplexer_13_out_7);
  not not_78 (nWRD_DATout, demultiplexer_14_out_0);
  not not_79 (nMDR_DATout, demultiplexer_14_out_1);
  not not_80 (COND_N, demultiplexer_15_out_1);
  not not_81 (COND_Z, demultiplexer_15_out_2);
  not not_82 (CONV_V, demultiplexer_15_out_3);
  not not_83 (COND_C, demultiplexer_15_out_4);
  PullDown pulldown_5 (.out(pulldown_5_out));
  PullDown pulldown_6 (.out(pulldown_6_out));
  BusSplitter #(.Bits(16)) bussplitter_1 (
    .D(MEMDATA), .OE(MEM_dir), .D0(pulldown_5_out), .D1(pulldown_6_out), .D2(bussplitter_1_d2),
    .D3(bussplitter_1_d3), .D4(bussplitter_1_d4), .D5(bussplitter_1_d5), .D6(bussplitter_1_d6),
    .D7(bussplitter_1_d7), .D8(bussplitter_1_d8), .D9(bussplitter_1_d9), .D10(bussplitter_1_d10),
    .D11(bussplitter_1_d11), .D12(bussplitter_1_d12), .D13(bussplitter_1_d13), .D14(bussplitter_1_d14),
    .D15(bussplitter_1_d15));
  PullDown pulldown_7 (.out(bussplitter_1_d15));
  PullDown pulldown_8 (.out(bussplitter_1_d14));
  or or_3 (or_3_out, and_8_out, and_9_out);
  and and_13 (and_13_out, ~COND_C, ~FLAG_C);  // And
  PullDown pulldown_9 (.out(bussplitter_1_d2));
  PullDown pulldown_10 (.out(bussplitter_1_d3));
  PullDown pulldown_11 (.out(bussplitter_1_d4));
  PullDown pulldown_12 (.out(bussplitter_1_d5));
  PullDown pulldown_13 (.out(bussplitter_1_d13));
  PullDown pulldown_14 (.out(bussplitter_1_d12));
  PullDown pulldown_15 (.out(bussplitter_1_d11));
  PullDown pulldown_16 (.out(bussplitter_1_d10));
  or or_4 (or_4_out, and_10_out, and_13_out);
  PullDown pulldown_17 (.out(bussplitter_1_d6));
  PullDown pulldown_18 (.out(bussplitter_1_d7));
  PullDown pulldown_19 (.out(bussplitter_1_d9));
  PullDown pulldown_20 (.out(bussplitter_1_d8));
  // _74245 _74245_1: pin names not known; wires that end beside it: MEM_dir, 1'b1, 1'b0, pulldown_5_out, pulldown_6_out, bussplitter_1_d2, bussplitter_1_d3, bussplitter_1_d4, bussplitter_1_d5, bussplitter_1_d6, bussplitter_1_d7, nMEM_en, _74245_1_p13, _74245_1_p14, _74245_1_p15, _74245_1_p16, _74245_1_p17, _74245_1_p18, _74245_1_p19, _74245_1_p20
  // _74245 _74245_2: pin names not known; wires that end beside it: MEM_dir, 1'b1, 1'b0, bussplitter_1_d8, bussplitter_1_d9, bussplitter_1_d10, bussplitter_1_d11, bussplitter_1_d12, bussplitter_1_d13, bussplitter_1_d14, bussplitter_1_d15, nMEM_en, _74245_2_p13, _74245_2_p14, _74245_2_p15, _74245_2_p16, _74245_2_p17, _74245_2_p18, _74245_2_p19, _74245_2_p20
  or or_5 (or_5_out, or_3_out, or_4_out);
  PullDown pulldown_21 (.out(_74245_2_p20));
  PullDown pulldown_22 (.out(_74245_2_p19));
  PullDown pulldown_23 (.out(_74245_2_p18));
  not not_84 (not_84_out, or_5_out);
  PullDown pulldown_24 (.out(_74245_2_p17));
  PullDown pulldown_25 (.out(_74245_2_p16));
  PullDown pulldown_26 (.out(_74245_2_p15));
  PullDown pulldown_27 (.out(_74245_2_p14));
  assign COND_RES = ~COND_POS ? or_5_out : 1'bz;  // DriverInvSel driverinvsel_3
  assign COND_RES = ~COND_NEG ? not_84_out : 1'bz;  // DriverInvSel driverinvsel_4
  PullDown pulldown_28 (.out(_74245_2_p13));
  PullDown pulldown_29 (.out(_74245_1_p20));
  PullDown pulldown_30 (.out(_74245_1_p19));
  PullDown pulldown_31 (.out(_74245_1_p18));
  PullDown pulldown_32 (.out(_74245_1_p17));
  PullDown pulldown_33 (.out(_74245_1_p16));
  PullDown pulldown_34 (.out(_74245_1_p15));
  PullDown pulldown_35 (.out(_74245_1_p14));
  not not_85 (not_85_out, MEM_dir);
  BusSplitter #(.Bits(16)) bussplitter_2 (
    .D(DATA), .OE(not_85_out), .D0(_74245_1_p13), .D1(_74245_1_p14), .D2(_74245_1_p15), .D3(_74245_1_p16),
    .D4(_74245_1_p17), .D5(_74245_1_p18), .D6(_74245_1_p19), .D7(_74245_1_p20), .D8(_74245_2_p13),
    .D9(_74245_2_p14), .D10(_74245_2_p15), .D11(_74245_2_p16), .D12(_74245_2_p17), .D13(_74245_2_p18),
    .D14(_74245_2_p19), .D15(_74245_2_p20));
  PullDown pulldown_36 (.out(_74245_1_p13));
  LED D15 (.in(d_ff_1_q[15]));
  LED A15 (.in(d_ff_2_q[15]));
  DipSwitch _15 (.out(_15_out[15]));
  or or_6 (or_6_out, CLK2, TEMP_clr);
  LED D13 (.in(d_ff_1_q[13]));
  LED D14 (.in(d_ff_1_q[14]));
  LED A13 (.in(d_ff_2_q[13]));
  LED A14 (.in(d_ff_2_q[14]));
  DipSwitch _13 (.out(_15_out[13]));
  DipSwitch _14 (.out(_15_out[14]));
  Register #(.Bits(16)) A (.D(DATA), .C(CLK2), .en(~nA_st), .Q(A_q));
  Register #(.Bits(16)) B (.D(DATA), .C(CLK2), .en(~nB_st), .Q(B_q));
  Register #(.Bits(16)) C (.D(DATA), .C(CLK2), .en(~nC_st), .Q(C_q));
  Register #(.Bits(16)) D (.D(DATA), .C(CLK2), .en(~nD_st), .Q(D_q));
  Register #(.Bits(16)) E (.D(DATA), .C(CLK2), .en(~nE_st), .Q(E_q));
  LED D12 (.in(d_ff_1_q[12]));
  LED A12 (.in(d_ff_2_q[12]));
  DipSwitch _12 (.out(_15_out[12]));
  Register #(.Bits(16)) OP1 (.D(DATA), .C(CLK2), .en(~nOP1_st), .Q(OP1_q));
  CounterPreset #(.Bits(16)) OP2 (
    .en(~1'b1), .C(or_6_out), .dir(1'b0), .in(DATA), .ld(~nOP2_st), .clr(TEMP_clr), .out(OP2_out));  // open: ovf
  LED D11 (.in(d_ff_1_q[11]));
  LED A11 (.in(d_ff_2_q[11]));
  DipSwitch _11 (.out(_15_out[11]));
  LED D9 (.in(d_ff_1_q[9]));
  LED D10 (.in(d_ff_1_q[10]));
  LED A9 (.in(d_ff_2_q[9]));
  LED A10 (.in(d_ff_2_q[10]));
  DipSwitch _9 (.out(_15_out[9]));
  DipSwitch _10 (.out(_15_out[10]));
  assign DATA = ~nA_DATout ? A_q : 16'bz;  // DriverInvSel driverinvsel_5
  assign DATA = ~nB_DATout ? B_q : 16'bz;  // DriverInvSel driverinvsel_6
  assign DATA = ~nC_DATout ? C_q : 16'bz;  // DriverInvSel driverinvsel_7
  assign DATA = ~nD_DATout ? D_q : 16'bz;  // DriverInvSel driverinvsel_8
  assign DATA = ~nE_DATout ? E_q : 16'bz;  // DriverInvSel driverinvsel_9
  LED D8 (.in(d_ff_1_q[8]));
  LED A8 (.in(d_ff_2_q[8]));
  DipSwitch _8 (.out(_15_out[8]));
  PullDown #(.Bits(16)) pulldown_37 (.out(DATA));
  PullDown #(.Bits(16)) pulldown_38 (.out(DATA));
  PullDown #(.Bits(16)) pulldown_39 (.out(DATA));
  PullDown #(.Bits(16)) pulldown_40 (.out(DATA));
  PullDown #(.Bits(16)) pulldown_41 (.out(DATA));
  LED D7 (.in(d_ff_1_q[7]));
  LED A7 (.in(d_ff_2_q[7]));
  DipSwitch _7 (.out(_15_out[7]));
  LED D5 (.in(d_ff_1_q[5]));
  LED D6 (.in(d_ff_1_q[6]));
  LED A5 (.in(d_ff_2_q[5]));
  LED A6 (.in(d_ff_2_q[6]));
  DipSwitch _5 (.out(_15_out[5]));
  DipSwitch _6 (.out(_15_out[6]));
  ALU alu_1 (
    .Sum(alu_1_sum), .C_sel(\Σ_Csel ), .C_val(\Σ_Cval ), .nCin(FLAG_C), .A(OP1_q), .Sel(\Σ_sel ),
    .B(OP2_out), .M(\Σ_M ), .C_f(alu_1_c_f[3]), .N_f(alu_1_c_f[2]), .Z_f(alu_1_c_f[1]), .V_f(alu_1_c_f[0]));
  BarrelShifter #(.Bits(16)) barrelshifter_1 (.in(OP1_q), .shift(5'b00001), .out(barrelshifter_1_out));
  BarrelShifter #(.Bits(16), .direction("right")) barrelshifter_2 (
    .in(OP1_q), .shift(5'b00001), .out(barrelshifter_2_out));
  BitExtender bitextender_1 (.in(OP1_q[7:0]), .out(bitextender_1_out));
  LED D4 (.in(d_ff_1_q[4]));
  LED A4 (.in(d_ff_2_q[4]));
  DipSwitch _4 (.out(_15_out[4]));
  LED D3 (.in(d_ff_1_q[3]));
  and and_14 (and_14_out, CLK2, ~HLT_ack);  // And
  LED A3 (.in(d_ff_2_q[3]));
  and and_15 (and_15_out, CLK2, ~HLT_ack);  // And
  DipSwitch _3 (.out(_15_out[3]));
  assign driverinvsel_10_out = ~nF_DATin ? DATA[3:0] : 4'bz;  // DriverInvSel driverinvsel_10
  assign driverinvsel_10_out = ~nF_ALUin ? alu_1_c_f : 4'bz;  // DriverInvSel driverinvsel_11
  CounterPreset #(.Bits(16)) PC (
    .en(~nPC_en), .C(CLK2), .dir(1'b0), .in(DATA), .ld(~nPC_st), .clr(1'b0), .out(PC_out));  // open: ovf
  CounterPreset #(.Bits(16)) SP (
    .en(~nSP_en), .C(CLK2), .dir(REG_dir), .in(DATA), .ld(~nSP_st), .clr(1'b0), .out(SP_out));  // open: ovf
  CounterPreset #(.Bits(16)) X (
    .en(~nX_en), .C(CLK2), .dir(REG_dir), .in(DATA), .ld(~nX_st), .clr(1'b0), .out(X_out));  // open: ovf
  CounterPreset #(.Bits(16)) Y (
    .en(~nY_en), .C(CLK2), .dir(REG_dir), .in(DATA), .ld(~nY_st), .clr(1'b0), .out(Y_out));  // open: ovf
  LED D1 (.in(d_ff_1_q[1]));
  LED D2 (.in(d_ff_1_q[2]));
  D_FF #(.Bits(16)) d_ff_1 (.D(DATA), .C(and_14_out), .Q(d_ff_1_q));  // open: nQ
  LED A1 (.in(d_ff_2_q[1]));
  LED A2 (.in(d_ff_2_q[2]));
  D_FF #(.Bits(16)) d_ff_2 (.D(ADDRESS), .C(and_15_out), .Q(d_ff_2_q));  // open: nQ
  DipSwitch _1 (.out(_15_out[1]));
  DipSwitch _2 (.out(_15_out[2]));
  PullDown #(.Bits(4)) pulldown_42 (.out(driverinvsel_10_out));
  assign DATA = ~nLSH_DATout ? barrelshifter_1_out : 16'bz;  // DriverInvSel driverinvsel_12
  PullDown #(.Bits(16)) pulldown_43 (.out(DATA));
  assign DATA = ~nRSH_DATout ? barrelshifter_2_out : 16'bz;  // DriverInvSel driverinvsel_13
  PullDown #(.Bits(16)) pulldown_44 (.out(DATA));
  assign DATA = ~nSEX_DATout ? bitextender_1_out : 16'bz;  // DriverInvSel driverinvsel_14
  PullDown #(.Bits(16)) pulldown_45 (.out(DATA));
  LED D0 (.in(d_ff_1_q[0]));
  LED A0 (.in(d_ff_2_q[0]));
  assign DATA = ~1'b1 ? _15_out : 16'bz;  // DriverInvSel driverinvsel_15
  DipSwitch _0 (.out(_15_out[0]));
  assign ADDRESS = ~nPC_ADSout ? PC_out : 16'bz;  // DriverInvSel driverinvsel_16
  assign ADDRESS = ~nSP_ADSout ? SP_out : 16'bz;  // DriverInvSel driverinvsel_17
  assign DATA = ~nX_DATout ? X_out : 16'bz;  // DriverInvSel driverinvsel_18
  assign DATA = ~nY_DATout ? Y_out : 16'bz;  // DriverInvSel driverinvsel_19
  LED V (.in(FLAG_V));
  LED C_2 (.in(not_86_out));
  not not_86 (not_86_out, FLAG_C);
  assign HLT = ~nPAN_HLTen ? RUN_out : 1'bz;  // DriverInvSel driverinvsel_20
  DipSwitch RUN (.out(RUN_out));
  Register #(.Bits(2)) NZ_F (.D(driverinvsel_10_out[1:0]), .C(CLK2), .en(~nNZ_Fst), .Q(FLAG_NZ));
  Register V_F (.D(driverinvsel_10_out[2]), .C(CLK2), .en(~nV_Fst), .Q(FLAG_V));
  Register nC_F (.D(driverinvsel_10_out[3]), .C(CLK2), .en(~nC_Fst), .Q(FLAG_C));
  assign DATA = ~nPC_DATout ? PC_out : 16'bz;  // DriverInvSel driverinvsel_21
  PullDown #(.Bits(16)) pulldown_46 (.out(DATA));
  assign DATA = ~nSP_DATout ? SP_out : 16'bz;  // DriverInvSel driverinvsel_22
  PullDown #(.Bits(16)) pulldown_47 (.out(DATA));
  PullDown #(.Bits(16)) pulldown_48 (.out(DATA));
  PullDown #(.Bits(16)) pulldown_49 (.out(DATA));
  LED Z (.in(FLAG_NZ[1]));
  DipSwitch STEP (.out(STP));
  PullDown #(.Bits(16)) pulldown_50 (.out(ADDRESS));
  PullDown #(.Bits(16)) pulldown_51 (.out(ADDRESS));
  LED N (.in(FLAG_NZ[0]));
  Register #(.Bits(16)) MDR (.D(DATA), .C(CLK2), .en(~nMDR_st), .Q(MDR_q));
  or or_7 (or_7_out, CLK2, TEMP_clr);
  or or_8 (or_8_out, CLK2, TEMP_clr);
  assign DATA = ~nSUM_DATout ? alu_1_sum : 16'bz;  // DriverInvSel driverinvsel_23
  PullDown #(.Bits(16)) pulldown_52 (.out(DATA));
  assign DATA = ~nF_DATout ? {{11{1'b0}}, IRQ_FTdat, FLAG_C, FLAG_V, FLAG_NZ} : 16'bz;  // DriverInvSel driverinvsel_24
  PullDown #(.Bits(16)) pulldown_53 (.out(DATA));
  CounterPreset #(.Bits(8)) MARH (
    .en(~1'b1), .C(or_7_out), .dir(1'b0), .in(DATA[15:8]), .ld(~nMARH_st), .clr(TEMP_clr), .out(MARH_out));  // open: ovf
  CounterPreset #(.Bits(8)) MARL (
    .en(~1'b1), .C(or_8_out), .dir(1'b0), .in(DATA[7:0]), .ld(~nMARL_st), .clr(TEMP_clr), .out(MARL_out));  // open: ovf
  assign DATA = ~nMDR_DATout ? MDR_q : 16'bz;  // DriverInvSel driverinvsel_25
  PullDown #(.Bits(16)) pulldown_54 (.out(DATA));
  assign ADDRESS = ~nMAR_ADSout ? {MARH_out, MARL_out} : 16'bz;  // DriverInvSel driverinvsel_26
  PullDown #(.Bits(16)) pulldown_55 (.out(ADDRESS));
  not not_87 (not_87_out, STP);
  // _7474 _7474_2: pin names not known; wires that end beside it: not_87_out, 1'b0, 1'b0, HLT_ack, 1'b0, 1'b0, 1'b0, 1'b0, 1'b1, 1'b0, nPAN_HLTen
  // Pins of 12 and 16 bits meet at pulldown_2_out

  // Other names for the same wires on the sheet: CLK_1 = CLK1; CLK_2 = CLK2

  // Notes on the sheet:
  //   Clock: Hz: 2
  //   Control Sequencing
  //   Control Decoding
  //   Memory/IRQ
  //   contents of µCODE (hex, n*v repeats v):
  //   619000009ec,10000a008,100000209,601000009ef,80200000229,11*0,16*3000000000
  //   ,619000009ec,8240000000,14*0,16*3000000000,619000009ec,200000000
  //   ,14*0,16*3000000000,619000009ec,8240000000,14*0,16*3000000000
  //   ,619000009ec,140000000,601000009ed,140000000,40100000550,60120000de9
  //   ,40100000510,61e200009ec,8*0,48*3000000000,619000009ec,240000000
  //   ,14*0,16*3000000000,619000009ec,8240000000,14*0,16*3000000000
  //   ,619000009ec,240000000,14*0,16*3000000000,619000009ec,8240000000
  //   ,14*0,16*3000000000,619000009ec,240000000,14*0,16*3000000000,619000009ec
  //   ,8240000000,14*0,16*3000000000,619000009ec,240000000,14*0,16*3000000000
  //   ,619000009ec,8240000000,14*0,16*3000000000,619000009ec,240000000
  //   ,14*0,16*3000000000,619000009ec,8240000000,14*0,16*3000000000
  //   ,619000009ec,240000000,14*0,16*3000000000,619000009ec,8240000000
  //   ,14*0,16*3000000000,619000009ec,240000000,14*0,16*3000000000,619000009ec
  //   ,8240000000,14*0,16*3000000000,619000009ec,240000000,14*0,16*3000000000
  //   ,619000009ec,8240000000,14*0,16*3000000000,619000009ec,240000000
  //   ,14*0,16*3000000000,619000009ec,8240000000,14*0,16*3000000000
  //   ,619000009ec,240000000,14*0,16*3000000000,619000009ec,8240000000
  //   ,14*0,16*3000000000,619000009ec,240000000,14*0,16*3000000000,619000009ec
  //   ,8240000000,14*0,16*3000000000,619000009ec,240000000,14*0,16*3000000000
  //   ,619000009ec,8240000000,14*0,16*3000000000,619000009ec,8240000000
  //   ,14*0,16*3000000000,619000009ec,8240000000,14*0,16*3000000000
  //   ,619000009ec,240000000,14*0,16*3000000000,619000009ec,8240000000
  //   ,14*0,16*3000000000,619000009ec,140000000,601000009ef,200000229
  //   ,12*0,16*3000000000,619000009ec,8240000000,14*0,16*3000000000
  //   ,619000009ec,10000014a,140000000,601000009eb,204900169,11*0,16*3000000000
  //   ,619000009ec,8240000000,14*0,16*3000000000,619000009ec,140000000
  //   ,10000002a,601000009eb,204900169,11*0,16*3000000000,619000009ec
  //   ,8240000000,14*0,16*3000000000,619000009ec,140000000,10000004a
  //   ,601000009eb,204900169,11*0,16*3000000000,619000009ec,8240000000
  //   ,14*0,16*3000000000,619000009ec,140000000,10000006a,601000009eb
  //   ,204900169,11*0,16*3000000000,619000009ec,8240000000,14*0,16*3000000000
  //   ,619000009ec,140000000,10000008a,601000009eb,204900169,11*0,16*3000000000
  //   ,619000009ec,8240000000,14*0,16*3000000000,619000009ec,140000000
  //   ,1000000aa,601000009eb,204900169,11*0,16*3000000000,619000009ec
  //   ,8240000000,14*0,16*3000000000,619000009ec,140000000,1000000ca
  //   ,601000009eb,204900169,11*0,16*3000000000,619000009ec,8240000000
  //   ,14*0,16*3000000000,619000009ec,140000000,1000000ea,601000009eb
  //   ,204900169,11*0,16*3000000000,619000009ec,8240000000,14*0,16*3000000000
  //   ,619000009ec,240000000,14*0,16*3000000000,619000009ec,8240000000
  //   ,14*0,16*3000000000,619000009ec,240000000,14*0,16*3000000000,619000009ec
  //   ,8240000000,14*0,16*3000000000,619000009ec,240000000,14*0,16*3000000000
  //   ,619000009ec,8240000000,14*0,16*3000000000,619000009ec,240000000
  //   ,14*0,16*3000000000,619000009ec,8240000000,14*0,16*3000000000
  //   ,619000009ec,240000000,14*0,16*3000000000,619000009ec,8240000000
  //   ,14*0,16*3000000000,619000009ec,130000000,602000005e9,13*0,16*3000000000
  //   ,619000009ec,8240000000,14*0,16*3000000000,619000009ec,240000000
  //   ,14*0,16*3000000000,619000009ec,8240000000,14*0,16*3000000000
  //   ,619000009ec,240000000,14*0,16*3000000000,619000009ec,8240000000
  //   ,14*0,16*3000000000,619000009ec,240000000,14*0,16*3000000000,619000009ec
  //   ,8240000000,14*0,16*3000000000,619000009ec,240000000,14*0,16*3000000000
  //   ,619000009ec,8240000000,14*0,16*3000000000,619000009ec,240000000
  //   ,14*0,16*3000000000,619000009ec,8240000000,14*0,16*3000000000
  //   ,619000009ec,240000000,14*0,16*3000000000,619000009ec,8240000000
  //   ,14*0,16*3000000000,619000009ec,240000000,14*0,16*3000000000,619000009ec
  //   ,8240000000,14*0,16*3000000000,619000009ec,240000000,14*0,16*3000000000
  //   ,619000009ec,8240000000,14*0,16*3000000000,619000009ec,240000000
  //   ,14*0,16*3000000000,619000009ec,8240000000,14*0,16*3000000000
  //   ,619000009ec,240000000,14*0,16*3000000000,619000009ec,8240000000
  //   ,14*0,16*3000000000,619000009ec,240000000,14*0,16*3000000000,619000009ec
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  //   contents of ROM_16x64k (hex, n*v repeats v):
  //   57328*0,16*25,40,1,40,1,8187*0,e000
  //   ALU
  //   Registers
  //   Control Panel
  //   ATLAS CPU-16
  //   By Hayden B.
endmodule
